# Fritzing sketch cwPaddle2USBandBluetooth (saved by Fritzing 1.0.2b)
breadboards: 1

parts:
  U1 = Waveshare ESP32-S3-Zero
  S1=Dot_(dit) = Pushbutton [package="[THT]"]
  S2=Dash_(dah) = Pushbutton [package="[THT]"]

nets:
  N1: U1.GND, S1=Dot_(dit).Pin_3, S1=Dot_(dit).Pin_4, S2=Dash_(dah).Pin_3, S2=Dash_(dah).Pin_4
  N2: U1.GP3, S1=Dot_(dit).Pin_1, S1=Dot_(dit).Pin_2
  N3: U1.GP5, S2=Dash_(dah).Pin_1, S2=Dash_(dah).Pin_2

notes:
  Power Supply via USB-C connector

custom parts:
  Waveshare ESP32-S3-Zero: Waveshare ESP32-S3-Zero mini development board, 23.5 x 18 mm, USB-C, 4 MB flash, 2 MB PSRAM, WS2812 RGB LED on GPIO21, BOOT button on GPIO0. 2x9 header holes (2.54 mm pitch, 15.24 mm row spacing) plus 3 top pads and 8 bottom pads.
